// Digital circuit 2bitmultiplier.dig as structural Verilog
module _2bitmultiplier (
  input  A_1,
  input  B_0,
  input  A_0,
  input  B_1
);

  wire and_1_out, and_2_out, and_3_out, and_4_out, and_5_out, and_6_out, and_7_out, and_8_out, not_1_out,
       not_2_out, not_3_out, not_4_out, not_5_out, not_6_out, or_1_out, or_2_out, or_3_out, or_4_out;

  and and_1 (and_1_out, A_1, A_0, B_1, B_0);
  and and_2 (and_2_out, A_1, not_1_out, B_1);
  not not_1 (not_1_out, A_0);
  and and_3 (and_3_out, A_1, B_1, not_2_out);
  not not_2 (not_2_out, B_0);
  not not_3 (not_3_out, A_0);
  not not_4 (not_4_out, B_1);
  not not_5 (not_5_out, A_1);
  not not_6 (not_6_out, B_0);
  or or_1 (or_1_out, and_2_out, and_3_out);
  and and_4 (and_4_out, A_1, not_3_out, B_0);
  and and_5 (and_5_out, A_1, not_4_out, B_0);
  and and_6 (and_6_out, not_5_out, A_0, B_1);
  and and_7 (and_7_out, A_0, B_1, not_6_out);
  or or_2 (or_2_out, and_4_out, and_5_out);
  or or_3 (or_3_out, and_6_out, and_7_out);
  or or_4 (or_4_out, or_2_out, or_3_out);
  and and_8 (and_8_out, A_0, B_0);
  LED P_3 (.in(and_1_out));
  LED P_2 (.in(or_1_out));
  LED P_1 (.in(or_4_out));
  LED P_0 (.in(and_8_out));
endmodule
