// Digital circuit 4bit-processor.dig as structural Verilog
module _4bit_processor (
  input  CLK,
  input  [1:0] IR_ctrl,
  input  [1:0] PC_ctrl,
  input  [1:0] Mem_ctrl,
  input  [3:0] Mem_in,
  output [3:0] PC_out,
  output [15:0] instr_16bit
);

  wire [3:0] register_file_1_p4, register_file_1_p7, register_file_1_p8;
  wire [7:0] registerfile_write_ctrl_1_write_ctrl;

  data_path_4_bit_processor data_path_4_bit_processor_1 (
    .IR_ctrl(IR_ctrl), .PC_ctrl(PC_ctrl), .instr_mem_ctrl(Mem_ctrl), .instr_mem_input(Mem_in), .CLK(CLK),
    .out(instr_16bit), .PC_out(PC_out));
  RegisterFile_Write_ctrl registerfile_write_ctrl_1 (
    .OpCode3(instr_16bit[1:0]), .write_ctrl(registerfile_write_ctrl_1_write_ctrl));
  // Register_file register_file_1: pin names not known; wires that end beside it: instr_16bit[3:2], instr_16bit[5:4], CLK, register_file_1_p4, instr_16bit[1:0], registerfile_write_ctrl_1_write_ctrl, register_file_1_p7, register_file_1_p8
  ALU alu_1 (
    .A(register_file_1_p7), .B(register_file_1_p8), .S1_S0_C_in(instr_16bit[8:6]), .D(register_file_1_p4));  // open: flag
endmodule
