// Digital circuit DRAM.dig as structural Verilog
module DRAM (
  input  clk,
  input  [3:0] Address,
  input  [3:0] Input_Mem,
  input  [1:0] ctrl_MEM_Load__Store__Reset,
  input  [1:0] ctrl_IR,
  input  PC_orind,
  input  [1:0] ctrl_PC_Load__INC__Reset,
  output [3:0] \output 
);

  wire [3:0] memory_1_output, multiplexer_1_out, pc_1_output;

  Multiplexer #(.Bits(4)) multiplexer_1 (.sel(PC_orind), .in_0(pc_1_output), .in_1(Address), .out(multiplexer_1_out));
  memory memory_1 (
    .clk(clk), .\input (Input_Mem), .CTRL(ctrl_MEM_Load__Store__Reset), .Address(multiplexer_1_out),
    .\output (memory_1_output));
  PC pc_1 (.clk(clk), .CTRL(ctrl_PC_Load__INC__Reset), .\output (pc_1_output));
  IR ir_1 (.clk(clk), .in(memory_1_output), .CTRL(ctrl_IR), .out(\output ));
  // Pins of 1 and 2 bits meet at ctrl_IR
endmodule
