// Digital circuit PC.dig as structural Verilog
module PC (
  input  clk,
  input  [1:0] CTRL,
  output [3:0] \output 
);

  wire _4bitadder_1_flag;
  wire [3:0] _4bitadder_1_sum, multiplexer_1_out, not_1_out;

  _4bitadder _4bitadder_1 (.A(\output ), .B(4'b0001), .C_in(1'b0), .flag(_4bitadder_1_flag), .sum(_4bitadder_1_sum));
  LED led_1 (.in(_4bitadder_1_flag));
  assign not_1_out = ~4'b0000;  // Not not_1, 4 bits wide
  Multiplexer #(.Selector_Bits(2), .Bits(4)) multiplexer_1 (
    .sel(CTRL), .in_0(\output ), .in_1(_4bitadder_1_sum), .in_2(4'b0000), .in_3(not_1_out),
    .out(multiplexer_1_out));
  D_FF d_ff_1 (.D(multiplexer_1_out[3]), .C(clk), .Q(\output [3]));  // open: nQ
  D_FF d_ff_2 (.D(multiplexer_1_out[2]), .C(clk), .Q(\output [2]));  // open: nQ
  D_FF d_ff_3 (.D(multiplexer_1_out[1]), .C(clk), .Q(\output [1]));  // open: nQ
  D_FF d_ff_4 (.D(multiplexer_1_out[0]), .C(clk), .Q(\output [0]));  // open: nQ
endmodule
