// Digital circuit data-path-4-bit-processor.dig as structural Verilog
module data_path_4_bit_processor (
  input  [1:0] IR_ctrl,
  input  [1:0] PC_ctrl,
  input  [1:0] instr_mem_ctrl,
  input  [3:0] instr_mem_input,
  input  CLK,
  output [15:0] out,
  output [3:0] PC_out
);

  wire and_1_out, not_1_out, not_2_out;
  wire [1:0] demultiplexer_1_out_0, demultiplexer_1_out_1, demultiplexer_1_out_2, demultiplexer_1_out_3;
  wire [3:0] demultiplexer_2_out_0, demultiplexer_2_out_1, demultiplexer_2_out_2, demultiplexer_2_out_3,
       ir_1_out, ir_2_out, ir_3_out, ir_4_out, memory_1_output;

  PC pc_1 (.clk(CLK), .CTRL(PC_ctrl), .\output (PC_out));
  memory memory_1 (
    .clk(CLK), .\input (instr_mem_input), .CTRL(instr_mem_ctrl), .Address(PC_out), .\output (memory_1_output));
  Demultiplexer #(.Selector_Bits(2), .Bits(2)) demultiplexer_1 (
    .sel(PC_out[1:0]), .in(IR_ctrl), .out_0(demultiplexer_1_out_0), .out_1(demultiplexer_1_out_1),
    .out_2(demultiplexer_1_out_2), .out_3(demultiplexer_1_out_3));
  Demultiplexer #(.Selector_Bits(2), .Bits(4)) demultiplexer_2 (
    .sel(PC_out[1:0]), .in(memory_1_output), .out_0(demultiplexer_2_out_0), .out_1(demultiplexer_2_out_1),
    .out_2(demultiplexer_2_out_2), .out_3(demultiplexer_2_out_3));
  not not_1 (not_1_out, PC_out[0]);
  not not_2 (not_2_out, PC_out[1]);
  and and_1 (and_1_out, not_1_out, not_2_out);
  IR ir_1 (.clk(CLK), .in(demultiplexer_2_out_0), .CTRL(demultiplexer_1_out_0), .out(ir_1_out));
  IR ir_2 (.clk(CLK), .in(demultiplexer_2_out_1), .CTRL(demultiplexer_1_out_1), .out(ir_2_out));
  IR ir_3 (.clk(CLK), .in(demultiplexer_2_out_2), .CTRL(demultiplexer_1_out_2), .out(ir_3_out));
  IR ir_4 (.clk(CLK), .in(demultiplexer_2_out_3), .CTRL(demultiplexer_1_out_3), .out(ir_4_out));
  assign out = and_1_out ? {ir_4_out, ir_3_out, ir_2_out, ir_1_out} : 16'bz;  // Driver driver_1
endmodule
