// Digital circuit 4bitadder.dig as structural Verilog
module _4bitadder (
  input  [3:0] A,
  input  [3:0] B,
  input  C_in
);

  wire fulladder_1_c_out, fulladder_1_sum, fulladder_2_c_out, fulladder_2_sum, fulladder_3_c_out,
       fulladder_3_sum, fulladder_4_c_out, fulladder_4_sum;

  fulladder fulladder_1 (
    .A(A[3]), .B(B[3]), .C_in(fulladder_2_c_out), .Sum(fulladder_1_sum), .C_out(fulladder_1_c_out));
  LED S3 (.in(fulladder_1_sum));
  LED C_out (.in(fulladder_1_c_out));
  fulladder fulladder_2 (
    .A(A[2]), .B(B[2]), .C_in(fulladder_3_c_out), .Sum(fulladder_2_sum), .C_out(fulladder_2_c_out));
  LED S2 (.in(fulladder_2_sum));
  fulladder fulladder_3 (
    .A(A[1]), .B(B[1]), .C_in(fulladder_4_c_out), .Sum(fulladder_3_sum), .C_out(fulladder_3_c_out));
  LED S1 (.in(fulladder_3_sum));
  fulladder fulladder_4 (.A(A[0]), .B(B[0]), .C_in(C_in), .Sum(fulladder_4_sum), .C_out(fulladder_4_c_out));
  LED S0 (.in(fulladder_4_sum));
endmodule
