// Digital circuit 4bitadder.dig as structural Verilog
module _4bitadder (
  input  [3:0] A,
  input  [3:0] B,
  input  C_in,
  output [3:0] sum,
  output C_out
);

  wire fulladder_1_c_out, fulladder_2_c_out, fulladder_3_c_out;

  fulladder fulladder_1 (.A(A[0]), .B(B[0]), .C_in(C_in), .Sum(sum[0]), .C_out(fulladder_1_c_out));
  fulladder fulladder_2 (.A(A[1]), .B(B[1]), .C_in(fulladder_1_c_out), .Sum(sum[1]), .C_out(fulladder_2_c_out));
  fulladder fulladder_3 (.A(A[2]), .B(B[2]), .C_in(fulladder_2_c_out), .Sum(sum[2]), .C_out(fulladder_3_c_out));
  fulladder fulladder_4 (.A(A[3]), .B(B[3]), .C_in(fulladder_3_c_out), .Sum(sum[3]), .C_out(C_out));
endmodule
