// Digital circuit Register_File.dig as structural Verilog
module Register_File (
  input  [1:0] Select_read1,
  input  [1:0] Select_read2,
  input  CLK,
  input  [3:0] Write_data,
  input  [1:0] Select_registers,
  input  [7:0] ctrl_registers,
  output [3:0] Read_data_1,
  output [3:0] Read_data_2
);

  wire [3:0] demultiplexer_1_out_0, demultiplexer_1_out_1, demultiplexer_1_out_2, demultiplexer_1_out_3,
       R_0_out, R_1_out, R_2_out, R_3_out;

  Demultiplexer #(.Bits(4), .Selector_Bits(2)) demultiplexer_1 (
    .sel(Select_registers), .in(Write_data), .out_0(demultiplexer_1_out_0), .out_1(demultiplexer_1_out_1),
    .out_2(demultiplexer_1_out_2), .out_3(demultiplexer_1_out_3));
  GPR R_0 (.clk(CLK), .in(demultiplexer_1_out_0), .CTRL(ctrl_registers[1:0]), .out(R_0_out));
  GPR R_1 (.clk(CLK), .in(demultiplexer_1_out_1), .CTRL(ctrl_registers[3:2]), .out(R_1_out));
  GPR R_2 (.clk(CLK), .in(demultiplexer_1_out_2), .CTRL(ctrl_registers[5:4]), .out(R_2_out));
  GPR R_3 (.clk(CLK), .in(demultiplexer_1_out_3), .CTRL(ctrl_registers[7:6]), .out(R_3_out));
  Multiplexer #(.Bits(4), .Selector_Bits(2)) multiplexer_1 (
    .sel(Select_read1), .in_0(R_0_out), .in_1(R_1_out), .in_2(R_2_out), .in_3(R_3_out), .out(Read_data_1));
  Multiplexer #(.Selector_Bits(2), .Bits(4)) multiplexer_2 (
    .sel(Select_read2), .in_0(R_0_out), .in_1(R_1_out), .in_2(R_2_out), .in_3(R_3_out), .out(Read_data_2));
endmodule
